// Digital circuit ALU.dig as structural Verilog
module ALU (
  input  [31:0] B,
  input  [31:0] A,
  input  [2:0] ALUControl,
  output [31:0] Result,
  output Z
);

  wire [31:0] add_1_s, and_1_out, multiplexer_1_out, not_1_out, or_1_out;

  Multiplexer #(.Bits(32)) multiplexer_1 (.sel(ALUControl[0]), .in_0(B), .in_1(not_1_out), .out(multiplexer_1_out));
  assign not_1_out = ~B;  // Not not_1, 32 bits wide
  assign and_1_out = A & multiplexer_1_out;  // And and_1, 32 bits wide
  assign or_1_out = A | multiplexer_1_out;  // Or or_1, 32 bits wide
  Add #(.Bits(32)) add_1 (.a(A), .b(multiplexer_1_out), .c_i(ALUControl[0]), .s(add_1_s));  // open: c_o
  Multiplexer #(.Selector_Bits(2), .Bits(32)) multiplexer_2 (
    .sel(ALUControl[2:1]), .in_0(add_1_s), .in_1(add_1_s), .in_2(and_1_out), .in_3(or_1_out), .out(Result));
  nor nor_1 (Z, Result[0], Result[1], Result[2], Result[3], Result[4], Result[5], Result[6], Result[7], Result[8], Result[9], Result[10], Result[11], Result[12], Result[13], Result[14], Result[15], Result[17], Result[18], Result[19], Result[20], Result[21], Result[22], Result[23], Result[24], Result[25], Result[26], Result[27], Result[28], Result[29], Result[30], Result[31], Result[16]);
endmodule
