// Digital circuit ALUControl.dig as structural Verilog
module ALUControl (
  input  [31:0] Instr,
  output [2:0] ALUControl,
  output RegWrite,
  output [4:0] InsType,
  output MemWrite
);

  and and_1 (RegWrite, ~Instr[2], ~Instr[3], ~Instr[4], ~Instr[5], ~Instr[6], ~Instr[12], Instr[13], ~Instr[14]);  // And
  and and_2 (MemWrite, ~Instr[2], ~Instr[3], ~Instr[4], Instr[5], ~Instr[6], ~Instr[12], Instr[13], ~Instr[14]);  // And
  or or_1 (InsType[1], RegWrite, 1'b0);
  assign ALUControl = RegWrite ? 3'b000 : 3'bz;  // Driver driver_1
  or or_2 (InsType[2], MemWrite, 1'b0);
  assign ALUControl = MemWrite ? 3'b000 : 3'bz;  // Driver driver_2

  assign {InsType[4:3], InsType[0]} = 3'b000;

  // Other names for the same wires on the sheet: I_type = InsType[1]; S_type = InsType[2]

  // Notes on the sheet:
  //   I-type lw 
  //   op             funct3   funct6/7	
  //   0000011    010	      n.a.
  //   s-type sw 
  //   op             funct3   funct6/7	
  //   0100011    010	      n.a.
endmodule
