// Digital circuit Instruction field decoder.dig as structural Verilog
module Instruction_field_decoder (
  input  [4:0] InsType,
  input  [31:0] Ins,
  output [19:0] immed_20,
  output [11:0] immed_12,
  output [4:0] rd,
  output [4:0] rs2,
  output [4:0] rs1
);

  wire [6:0] driver_1_out;
  wire [14:0] driver_3_out, driver_4_out;
  wire [31:0] driver_5_out;

  assign {immed_20, rd, driver_1_out} = InsType[4] ? Ins : 32'bz;  // Driver driver_1
  assign {immed_20, rd, driver_1_out} = InsType[3] ? Ins : 32'bz;  // Driver driver_2
  assign {immed_12, rs1, driver_3_out[14:12], rd, driver_3_out[6:0]} = InsType[1] ? Ins : 32'bz;  // Driver driver_3
  assign {immed_12[11:5], rs2, rs1, driver_4_out[14:12], immed_12[4:0], driver_4_out[6:0]} = InsType[2] ? Ins : 32'bz;  // Driver driver_4
  assign {driver_5_out[31:25], rs2, rs1, driver_5_out[14:12], rd, driver_5_out[6:0]} = InsType[0] ? Ins : 32'bz;  // Driver driver_5
endmodule
