// Digital circuit PC.dig as structural Verilog
module PC (
  input  CLK,
  input  RST_PC,
  output [23:0] PC
);

  wire or_1_out;

  or or_1 (or_1_out, CLK, RST_PC);
  CounterPreset #(.Bits(22), .isProgramCounter("true")) counterpreset_1 (
    .en(1'b1), .C(or_1_out), .dir(1'b0), .in(22'h3ff), .ld(RST_PC), .clr(1'b0), .out(PC[23:2]));  // open: ovf

  assign PC[1:0] = 2'b00;
endmodule
