// Digital circuit ALUControl.dig as structural Verilog
module ALUControl (
  input  [31:0] Instr,
  output [2:0] ALUControl,
  output DMAControl,
  output RegWrite
);

  and and_1 (DMAControl, Instr[0], Instr[1], ~Instr[2], ~Instr[3], ~Instr[4], ~Instr[5], ~Instr[6], ~Instr[12], Instr[13], ~Instr[14]);  // And
  assign ALUControl = DMAControl ? 3'b000 : 3'bz;  // Driver driver_1

  assign RegWrite = DMAControl;

  // Notes on the sheet:
  //   I-type lw 
  //   op             funct3   funct6/7	
  //   0000011    010	      n.a.
endmodule
