// Digital circuit Register File.dig as structural Verilog
module Register_File (
  input  [4:0] A1,
  input  CLK,
  input  [31:0] WD3,
  output [31:0] RD1
);

  wire and_1_out, and_2_out;
  wire [31:0] register_1_q, register_2_q;

  and and_1 (and_1_out, ~A1[4], ~A1[3], A1[2], A1[1], ~A1[0]);  // And
  and and_2 (and_2_out, ~A1[4], A1[3], ~A1[2], ~A1[1], A1[0]);  // And
  Register #(.Bits(32)) register_1 (.D(WD3), .C(CLK), .en(and_1_out), .Q(register_1_q));
  Register #(.Bits(32)) register_2 (.D(WD3), .C(CLK), .en(and_2_out), .Q(register_2_q));
  Multiplexer #(.Selector_Bits(5), .Bits(32)) multiplexer_1 (
    .sel(A1), .in_0({32{1'b0}}), .in_1({32{1'b0}}), .in_2({32{1'b0}}), .in_3({32{1'b0}}), .in_4({32{1'b0}}),
    .in_5({32{1'b0}}), .in_6(register_1_q), .in_7({32{1'b0}}), .in_8({32{1'b0}}), .in_9(register_2_q),
    .in_10({32{1'b0}}), .in_11({32{1'b0}}), .in_12({32{1'b0}}), .in_13({32{1'b0}}), .in_14({32{1'b0}}),
    .in_15({32{1'b0}}), .in_16({32{1'b0}}), .in_17({32{1'b0}}), .in_18({32{1'b0}}), .in_19({32{1'b0}}),
    .in_20({32{1'b0}}), .in_21({32{1'b0}}), .in_22({32{1'b0}}), .in_23({32{1'b0}}), .in_24({32{1'b0}}),
    .in_25({32{1'b0}}), .in_26({32{1'b0}}), .in_27({32{1'b0}}), .in_28({32{1'b0}}), .in_29({32{1'b0}}),
    .in_30({32{1'b0}}), .in_31({32{1'b0}}), .out(RD1));
endmodule
