// Digital circuit main.dig as structural Verilog
module main (
  input  in_1
);

  wire CLK, RST_PC;
  wire [2:0] alucontrol_1_alucontrol;
  wire [4:0] rom_1_d_2, rom_1_d_3;
  wire [11:0] rom_1_d_4;
  wire [14:0] rom_1_d;
  wire [23:0] pc_1_pc;
  wire [31:0] bitextender_1_out, registerfile_1_da, undriven;

  PC pc_1 (.CLK(CLK), .PC(pc_1_pc), .RST_PC(RST_PC));
  ROM #(.AddrBits(24), .isProgramMemory("true"), .Bits(32)) rom_1 (
    .A(pc_1_pc), .sel(1'b1), .D({rom_1_d_4, rom_1_d_3, rom_1_d[14:12], rom_1_d_2, rom_1_d[6:0]}));
  Button button_1 (.out(RST_PC));
  Button button_2 (.out(CLK));
  BitExtender #(.inputBits(12), .outputBits(32)) bitextender_1 (.in(rom_1_d_4), .out(bitextender_1_out));
  ALUControl alucontrol_1 (
    .Instr({rom_1_d_4, rom_1_d_3, rom_1_d[14:12], rom_1_d_2, rom_1_d[6:0]}),
    .ALUControl(alucontrol_1_alucontrol));  // open: DMAControl, RegWrite
  RegisterFile #(.AddrBits(5), .Bits(32)) registerfile_1 (
    .Din(undriven), .we(in_1), .Rw(rom_1_d_2), .C(CLK), .Ra(rom_1_d_3), .Rb({5{1'b0}}), .Da(registerfile_1_da));  // open: Db
  ALU alu_1 (.A(registerfile_1_da), .B(bitextender_1_out), .ALUControl(alucontrol_1_alucontrol));  // open: Result, Z

  // Notes on the sheet:
  //   contents of rom_1 (hex, n*v repeats v):
  //   4096*0,ffc4a303
endmodule
