// Digital circuit main.dig as structural Verilog
module main (
);

  wire CLK, MemWrite, not_1_out, RegWrite, RST_PC;
  wire [2:0] ALUControl;
  wire [4:0] InsType, rd, rs1, rs2;
  wire [11:0] immed_12;
  wire [19:0] immed_20;
  wire [23:0] pc_1_pc;
  wire [31:0] alu_1_result, bitextender_1_out, Din, RD2, registerfile_1_da, rom_1_d;

  PC pc_1 (.CLK(CLK), .PC(pc_1_pc), .RST_PC(RST_PC));
  ROM #(.AddrBits(24), .isProgramMemory("true"), .Bits(32)) rom_1 (.A(pc_1_pc), .sel(1'b1), .D(rom_1_d));
  Button button_1 (.out(RST_PC));
  Button button_2 (.out(CLK));
  ALUControl alucontrol_1 (
    .Instr(rom_1_d), .ALUControl(ALUControl), .RegWrite(RegWrite), .InsType(InsType), .MemWrite(MemWrite));
  Instruction_field_decoder instruction_field_decoder_1 (
    .InsType(InsType), .Ins(rom_1_d), .rd(rd), .rs1(rs1), .rs2(rs2), .immed_12(immed_12), .immed_20(immed_20));
  BitExtender #(.inputBits(12), .outputBits(32)) bitextender_1 (.in(immed_12), .out(bitextender_1_out));
  RegisterFile #(.AddrBits(5), .Bits(32)) registerfile_1 (
    .Din(Din), .we(RegWrite), .Rw(rd), .C(CLK), .Ra(rs1), .Rb(rs2), .Da(registerfile_1_da), .Db(RD2));
  ALU alu_1 (.A(registerfile_1_da), .B(bitextender_1_out), .ALUControl(ALUControl), .Result(alu_1_result));  // open: Z
  not not_1 (not_1_out, MemWrite);
  RAMDualPort #(.AddrBits(24), .Bits(32)) ramdualport_1 (
    .A(alu_1_result[23:0]), .Din(RD2), .str(MemWrite), .C(CLK), .ld(not_1_out), .D(Din));

  // Notes on the sheet:
  //   contents of rom_1 (hex, n*v repeats v):
  //   4096*0,ffc4a303,0,0,0,64a423
endmodule
